# Fritzing sketch lightboxFritzingMaster (saved by Fritzing 0.4.3b)
breadboards: 1

parts:
  IC1 = IC, DIP package, 28 pins [chip_label=Atmega8 spacing=300mil]
  Power_plug1 = Power plug
  IC2 = IC, DIP package, 8 pins [chip_label=SN75176BP spacing=300mil]
  R1 = Resistor [resistance=220 package=THT]
  R2 = Resistor [resistance=2.2 package=THT]
  R2_2 = Resistor [resistance=3.3 package=THT]
  R2_3 = Resistor [resistance=3.3 package=THT]
  S1 = Pushbutton [package=THT]
  Q2 = Basic FET N-Channel Standing
  Q2_2 = Basic FET N-Channel Standing
  Q2_3 = Basic FET N-Channel Standing
  Q4 = Basic FET N-Channel [package="TO220 [THT]"]  # not connected
  R3 = ResistorStanding
  J1 = screw terminal, 3 pins
  C1 = Electrolytic Capacitor [package=THT]
  C2 = Ceramic Capacitor [package=THT]
  LED1 = Blue LED - 5mm
  LED2 = green LED - 5mm
  LED3 = Red LED - 5mm
  IC2_2 = IC, DIP package, 8 pins [chip_label=SN75176BP spacing=300mil]
  J1_2 = screw terminal, 6 pins
  R4 = Resistor [resistance=100 package=THT]

nets:
  N1: IC1.pin1, R1.Pin_1
  N2: IC1.pin2, IC2.pin1
  N3: IC1.pin3, IC2.pin4
  N4: IC1.pin4, S1.leg1
  N5: IC1.pin7, Power_plug1.VCC, IC2.pin8, R1.Pin_0, R2.Pin_1, R2_2.Pin_1, R2_3.Pin_1, C1.+, C2.pin_0, IC2_2.pin2, IC2_2.pin3, IC2_2.pin8, J1_2.pin6
  N6: IC1.pin8, Power_plug1.GND, IC2.pin2, IC2.pin3, IC2.pin5, S1.leg0, Q2.connector2, Q2_2.connector2, Q2_3.connector2, J1.pin3, C1.-, C2.pin_1, IC2_2.pin5, J1_2.pin5
  N7: IC1.pin15, Q2.connector0
  N8: IC1.pin16, Q2_2.connector0
  N9: IC1.pin17, Q2_3.connector0
  N10: IC2.pin6, J1.pin2, IC2_2.pin6, R4.Pin_1
  N11: IC2.pin7, J1.pin1, IC2_2.pin7, R4.Pin_0
  N12: R2.Pin_0, R3.connector1
  N13: R2_2.Pin_0, LED2.anode
  N14: R2_3.Pin_0, LED1.anode
  N15: Q2.connector1, LED3.cathode
  N16: Q2_2.connector1, LED2.cathode
  N17: Q2_3.connector1, LED1.cathode
  N18: R3.connector0, LED3.anode
  N19: IC2_2.pin1, J1_2.pin3
  N20: IC2_2.pin4, J1_2.pin4

notes:
  Taster
  DC Buchse
  Zur RJ45-Buchse
  MOS-Fet N Channel
  Ansicht von oben
  --------------------------------
  Metallseite oben
  Beschriftete Seite unten
  =============>
  Die LEDs repräsentieren die
  3W LEDs auf dem Kühlkörper.
  2W widerstaende fuer leds
  rot: 2x 2,2ohm in reihe
  gruen: 3,3ohm
  blau: 3,3ohm
  Pollin
  Wandler RS232-TTL
  100ohm abschlusswiderstand
  fuer RS485
